# Fritzing sketch 7x5_with_shift_register (saved by Fritzing 0.9.2b)
breadboards: 1

parts:
  Part10 = Arduino Uno (Rev3)
  S1 = Pushbutton [package="[THT]"]
  LED1 = LED - 5mm [color="Red (633nm)" package="5 mm [THT]"]
  LED2 = LED - 5mm [color="Red (633nm)" package="5 mm [THT]"]
  LED3 = LED - 5mm [color="Red (633nm)" package="5 mm [THT]"]
  LED4 = LED - 5mm [color="Red (633nm)" package="5 mm [THT]"]
  LED5 = LED - 5mm [color="Red (633nm)" package="5 mm [THT]"]
  LED6 = LED - 5mm [color="Red (633nm)" package="5 mm [THT]"]
  LED7 = LED - 5mm [color="Red (633nm)" package="5 mm [THT]"]
  R1 = Resistor [tolerance=±5% resistance=220 package=THT]
  R2 = Resistor [tolerance=±5% resistance=220 package=THT]
  R3 = Resistor [tolerance=±5% resistance=220 package=THT]
  R4 = Resistor [tolerance=±5% resistance=220 package=THT]
  R5 = Resistor [tolerance=±5% resistance=220 package=THT]
  R6 = Resistor [tolerance=±5% resistance=220 package=THT]
  R7 = Resistor [tolerance=±5% resistance=220 package=THT]
  LED8 = LED - 5mm [color="Red (633nm)" package="5 mm [THT]"]
  LED9 = LED - 5mm [color="Red (633nm)" package="5 mm [THT]"]
  LED10 = LED - 5mm [color="Red (633nm)" package="5 mm [THT]"]
  LED11 = LED - 5mm [color="Red (633nm)" package="5 mm [THT]"]
  LED12 = LED - 5mm [color="Red (633nm)" package="5 mm [THT]"]
  LED13 = LED - 5mm [color="Red (633nm)" package="5 mm [THT]"]
  LED14 = LED - 5mm [color="Red (633nm)" package="5 mm [THT]"]
  LED15 = LED - 5mm [color="Red (633nm)" package="5 mm [THT]"]
  LED16 = LED - 5mm [color="Red (633nm)" package="5 mm [THT]"]
  LED17 = LED - 5mm [color="Red (633nm)" package="5 mm [THT]"]
  LED18 = LED - 5mm [color="Red (633nm)" package="5 mm [THT]"]
  LED19 = LED - 5mm [color="Red (633nm)" package="5 mm [THT]"]
  LED20 = LED - 5mm [color="Red (633nm)" package="5 mm [THT]"]
  LED21 = LED - 5mm [color="Red (633nm)" package="5 mm [THT]"]
  LED22 = LED - 5mm [color="Red (633nm)" package="5 mm [THT]"]
  LED23 = LED - 5mm [color="Red (633nm)" package="5 mm [THT]"]
  LED24 = LED - 5mm [color="Red (633nm)" package="5 mm [THT]"]
  LED25 = LED - 5mm [color="Red (633nm)" package="5 mm [THT]"]
  LED26 = LED - 5mm [color="Red (633nm)" package="5 mm [THT]"]
  LED27 = LED - 5mm [color="Red (633nm)" package="5 mm [THT]"]
  LED28 = LED - 5mm [color="Red (633nm)" package="5 mm [THT]"]
  LED29 = LED - 5mm [color="Red (633nm)" package="5 mm [THT]"]
  LED30 = LED - 5mm [color="Red (633nm)" package="5 mm [THT]"]
  LED31 = LED - 5mm [color="Red (633nm)" package="5 mm [THT]"]
  LED32 = LED - 5mm [color="Red (633nm)" package="5 mm [THT]"]
  LED33 = LED - 5mm [color="Red (633nm)" package="5 mm [THT]"]
  LED34 = LED - 5mm [color="Red (633nm)" package="5 mm [THT]"]
  LED35 = LED - 5mm [color="Red (633nm)" package="5 mm [THT]"]
  Part11 = Shift Register Breakout - 74HC595
  U1 = M74HC238 [package=dil16]
  R8 = Resistor [tolerance=±5% resistance=220 package=THT]

nets:
  N1: Part10.D8, Part11.LATCH_CLOCK
  N2: Part10.D2, S1.Pin_1, S1.Pin_2, R8.Pin_0
  N3: Part10.D3_PWM, U1.A
  N4: Part10.D4, U1.B
  N5: Part10.D5_PWM, U1.C
  N6: Part10.D6_PWM, Part11.SERIAL_IN
  N7: Part10.D7, Part11.CLOCK
  5V: Part10.5V, S1.Pin_3, Part11.VCC, Part11./RESET, U1.G1, U1.VCC
  GND: Part10.GND, Part11.GND, Part11./OUTPUT_ENABLE, U1.~G2A, U1.~G2B, U1.GND, R8.Pin_1
  N8: LED1.cathode, R2.Pin_1, LED13.cathode, LED19.cathode, LED25.cathode, LED30.cathode
  N9: LED1.anode, LED2.anode, LED3.anode, LED4.anode, LED5.anode, LED6.anode, LED7.anode, U1.Y4
  N10: LED2.cathode, R3.Pin_1, LED10.cathode, LED18.cathode, LED26.cathode, LED31.cathode
  N11: LED3.cathode, R4.Pin_1, LED14.cathode, LED16.cathode, LED27.cathode, LED33.cathode
  N12: LED4.cathode, R1.Pin_1, LED11.cathode, LED21.cathode, LED24.cathode, LED32.cathode
  N13: LED5.cathode, R7.Pin_1, LED9.cathode, LED15.cathode, LED17.cathode, LED29.cathode
  N14: LED6.cathode, R5.Pin_1, LED8.cathode, LED20.cathode, LED22.cathode, LED35.cathode
  N15: LED7.cathode, R6.Pin_1, LED12.cathode, LED23.cathode, LED28.cathode, LED34.cathode
  N16: R1.Pin_0, Part11.QG
  N17: R2.Pin_0, Part11.QF
  N18: R3.Pin_0, Part11.QE
  N19: R4.Pin_0, Part11.QD
  N20: R5.Pin_0, Part11.QB
  N21: R6.Pin_0, Part11.QA
  N22: R7.Pin_0, Part11.QC
  N23: LED8.anode, LED9.anode, LED10.anode, LED11.anode, LED12.anode, LED13.anode, LED14.anode, U1.Y3
  N24: LED15.anode, LED16.anode, LED19.anode, LED21.anode, LED22.anode, LED23.anode, LED26.anode, U1.Y1
  N25: LED17.anode, LED18.anode, LED20.anode, LED24.anode, LED25.anode, LED27.anode, LED28.anode, U1.Y2
  N26: LED29.anode, LED30.anode, LED31.anode, LED32.anode, LED33.anode, LED34.anode, LED35.anode, U1.Y0
